# Fritzing sketch Hardware (saved by Fritzing 0.9.4)
stripboards: 1

parts:
  D1 = Rectifier Diode [part_number=1N4001 package="Melf DO-213 AB [SMD]"]
  12V = female pin header, 2 pins [form="♀ (female)"]
  Ledstrip_5V = female pin header, 3 pins [form="♀ (female)"]
  Temp = female pin header, 2 pins [form="♀ (female)"]  # not connected
  Color = female pin header, 2 pins [form="♀ (female)"]  # not connected

nets:
  N1: D1.anode, Ledstrip_5V.pin3
  N2: 12V.pin1, Ledstrip_5V.pin1
