# Fritzing sketch hardware (saved by Fritzing 0.9.3b)
stripboards: 1

parts:
  M1 = DOIT Esp32 DevKit v1 (30 pins long, 11 pins width) [part_number=ESP32S-PIN30]
  IRL540N = Basic FET N-Channel [package="D2Pak [SMD]"]
  DIM_OUT = female pin header, 2 pins [form="♀ (female)"]
  12V_IN = female pin header, 2 pins [form="♀ (female)"]
  D1 = Rectifier Diode [part_number=1N4001 package="300 mil [THT]"]
  RotEnc = ENCODER-QUADRATURE [package=encoder-16mm-quad]
  R-A = female pin header, 1 pin [form="♀ (female)"]
  part = female pin header, 1 pin [form="♀ (female)"]
  R-B = female pin header, 1 pin [form="♀ (female)"]
  R-C = female pin header, 1 pin [form="♀ (female)"]
  part_2 = female pin header, 1 pin [form="♀ (female)"]
  RotEncSw = Pushbutton [package=THT]

nets:
  GND: M1.GND, IRL540N.source, 12V_IN.pin2, RotEnc.C, R-C.pin1, part_2.pin1, RotEncSw.leg0
  N1: M1.D2, IRL540N.Gate
  N2: M1.D4, part.pin1, RotEncSw.leg1
  N3: M1.RX2, RotEnc.B, R-B.pin1
  N4: M1.TX2, RotEnc.A, R-A.pin1
  N5: M1.VIN, D1.cathode
  N6: IRL540N.drain, DIM_OUT.pin2
  N7: DIM_OUT.pin1, 12V_IN.pin1, D1.anode

custom parts:
  DOIT Esp32 DevKit v1 (30 pins long, 11 pins width): The DOIT Esp32 DevKit v1 is one of the development board created by DOIT to evaluate the ESP-WROOM-32 module. It is based on the ESP32 microcontroller that boasts Wifi, Bluetooth, Ethernet and Low Power support all in a single chip. (vanepp) made breadboard work, adjusted pin numbering and labels and reduced size of schematic and cleaned up pcb. This chip is 30pins long (2 x15) and 11 pins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
