# Fritzing sketch hardware-double (saved by Fritzing 1.0.4)
stripboards: 1

parts:
  M1 = DOIT Esp32 DevKit v1 (30 pins long, 11 pins width) [part_number=ESP32S-PIN30]
  IRL540N-1 = Basic FET N-Channel [package="D2Pak [SMD]"]
  p1 = female pin header, 1 pin [form="♀ (female)"]
  switch_1 = Pushbutton [package=THT]
  J2 = female pin header, 2 pins [form="♀ (female)" part_number=Lamp]
  J3 = female pin header, 2 pins [form="♀ (female)" part_number=Power]
  J4 = male pin header, 2 pins [form="♂ (male)" part_number=3v3]
  C1* = Electrolytic Capacitor [capacitance=47µF voltage=35V package="100 mil [THT, electrolytic]"]
  switch_2 = Pushbutton [package=THT]
  p2 = female pin header, 1 pin [form="♀ (female)"]
  IRL540N-2 = Basic FET N-Channel [package="D2Pak [SMD]"]
  J5 = female pin header, 2 pins [form="♀ (female)" part_number=Lamp]
  J1 = longpad pin header, 3 pins [form="long pad" part_number="Pololu 3v3"]

nets:
  N1: M1.3V3, J4.pin1
  N2: M1.GND, J3.pin1, C1*.-, J1.pin2
  N3: M1.D15, IRL540N-2.Gate
  N4: M1.D2, IRL540N-1.Gate
  N5: M1.D4, p1.pin1, switch_1.leg1
  N6: M1.RX2, switch_2.leg1, p2.pin1
  N7: IRL540N-1.drain, J2.pin1
  GND: IRL540N-1.source, switch_1.leg0, switch_2.leg0, IRL540N-2.source
  N8: J2.pin2, J3.pin2, C1*.+, J5.pin2, J1.pin1
  N9: J4.pin2, J1.pin3
  N10: IRL540N-2.drain, J5.pin1

notes:
  C1 optional with long power leads (to protect Pololu)

custom parts:
  DOIT Esp32 DevKit v1 (30 pins long, 11 pins width): The DOIT Esp32 DevKit v1 is one of the development board created by DOIT to evaluate the ESP-WROOM-32 module. It is based on the ESP32 microcontroller that boasts Wifi, Bluetooth, Ethernet and Low Power support all in a single chip. (vanepp) made breadboard work, adjusted pin numbering and labels and reduced size of schematic and cleaned up pcb. This chip is 30pins long (2 x15) and 11 pins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
