# Fritzing sketch hardware (saved by Fritzing 0.9.4)
stripboards: 1

parts:
  M1 = DOIT Esp32 DevKit v1 (30 pins long, 11 pins width) [part_number=ESP32S-PIN30]
  IRL540N = Basic FET N-Channel [package="D2Pak [SMD]"]
  Rotary_encoder_(optional) = ENCODER-QUADRATURE [package=encoder-16mm-quad]
  R-A = female pin header, 1 pin [form="♀ (female)"]
  part = female pin header, 1 pin [form="♀ (female)"]
  R-B = female pin header, 1 pin [form="♀ (female)"]
  R-C = female pin header, 1 pin [form="♀ (female)"]
  part_2 = female pin header, 1 pin [form="♀ (female)"]
  Rotary_Encoder_Switch_(optional) = Pushbutton [package=THT]
  J1 = longpad pin header, 3 pins [form="long pad" part_number="Pololu 3v3"]
  J2 = female pin header, 2 pins [form="♀ (female)" part_number=Lamp]
  J3 = female pin header, 2 pins [form="♀ (female)" part_number=Power]
  J4 = male pin header, 2 pins [form="♂ (male)" part_number=3v3]
  C1* = Electrolytic Capacitor [capacitance=47µF voltage=35V package="100 mil [THT, electrolytic]"]

nets:
  N1: M1.3V3, J1.pin3, J4.pin1, J4.pin2
  GND: M1.GND, IRL540N.source, Rotary_encoder_(optional).C, R-C.pin1, part_2.pin1, Rotary_Encoder_Switch_(optional).leg0, J1.pin2, J3.pin1, C1*.-
  N2: M1.D2, IRL540N.Gate
  N3: M1.D4, part.pin1, Rotary_Encoder_Switch_(optional).leg1
  N4: M1.RX2, Rotary_encoder_(optional).B, R-B.pin1
  N5: M1.TX2, Rotary_encoder_(optional).A, R-A.pin1
  N6: IRL540N.drain, J2.pin1
  N7: J1.pin1, J2.pin2, J3.pin2, C1*.+

notes:
  C1 optional with long power leads (to protect Pololu)

custom parts:
  DOIT Esp32 DevKit v1 (30 pins long, 11 pins width): The DOIT Esp32 DevKit v1 is one of the development board created by DOIT to evaluate the ESP-WROOM-32 module. It is based on the ESP32 microcontroller that boasts Wifi, Bluetooth, Ethernet and Low Power support all in a single chip. (vanepp) made breadboard work, adjusted pin numbering and labels and reduced size of schematic and cleaned up pcb. This chip is 30pins long (2 x15) and 11 pins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
