# Fritzing sketch Hardware-12v (saved by Fritzing 0.9.6b)
stripboards: 1

parts:
  D1 = Rectifier Diode [part_number=1N4001 package="Melf DO-213 AB [SMD]"]  # not connected
  12V = female pin header, 2 pins [form="♀ (female)" part_number="JST-BEC female"]
  Ledstrip_12V = female pin header, 3 pins [form="♀ (female)" part_number="JST-SM Female"]
  Temp = female pin header, 2 pins [form="♀ (female)"]  # not connected
  Level = female pin header, 2 pins [form="♀ (female)"]  # not connected
  IRL540N = Basic FET N-Channel [package="D2Pak [SMD]"]
  C1 = Electrolytic Capacitor [capacitance=1µF package="100 mil [THT, electrolytic]"]
  R1 = Resistor [tolerance=±5% resistance=10k power=0.25 package=THT]

nets:
  N1: 12V.pin1, IRL540N.source, C1.-, R1.Pin_0
  N2: 12V.pin2, Ledstrip_12V.pin3, C1.+
  N3: Ledstrip_12V.pin1, IRL540N.drain
  N4: IRL540N.Gate, R1.Pin_1

notes:
  This is the 12V Ledstrip circuit
