# Fritzing sketch Hardware-5v (saved by Fritzing 0.9.6b)
stripboards: 1

parts:
  D1 = Rectifier Diode [part_number=1N4001 package="Melf DO-213 AB [SMD]"]
  12V = female pin header, 2 pins [form="♀ (female)" part_number="JST-BEC female"]
  Ledstrip_5V = female pin header, 3 pins [form="♀ (female)" part_number="JST-SM Male"]
  Temp = female pin header, 2 pins [form="♀ (female)"]  # not connected
  Level = female pin header, 2 pins [form="♀ (female)"]  # not connected
  IRL540N = Basic FET N-Channel [package="D2Pak [SMD]"]
  C1 = Electrolytic Capacitor [capacitance=1µF package="100 mil [THT, electrolytic]"]
  R1 = Resistor [tolerance=±5% resistance=10k power=0.25 package=THT]
  R2 = Resistor [tolerance=±5% power=0.25 resistance=10k package=THT]
  R3 = Resistor [tolerance=±5% power=0.25 resistance=100k package=THT]

nets:
  N1: D1.anode, Ledstrip_5V.pin3
  N2: 12V.pin1, IRL540N.source, C1.-, R1.Pin_0
  N3: 12V.pin2, C1.+, R3.Pin_0
  N4: Ledstrip_5V.pin1, IRL540N.drain
  N5: IRL540N.Gate, R1.Pin_1
  N6: R2.Pin_0, R3.Pin_1

notes:
  This is the 5V Ledstrip circuit
